# Fritzing sketch Hardware_v1_emitterCircuit (saved by Fritzing 0.9.3b)
breadboards: 1

parts:
  U2 = Voltage Regulator - 5V [package="TO220 [THT]"]
  ARduino = Arduino Nano (Rev3.0) (ICSP)
  R1 = Resistor [tolerance=±5% resistance=120 package=THT]
  Q1 = Basic FET N-Channel [package="TO220 [THT]"]
  BAT1 = Battery Holders [package=battcon_20mm]

nets:
  24V: U2.input_voltage, BAT1.+
  GND: U2.GND, BAT1.-
  N1: U2.output_voltage, ARduino.VIN
  N2: ARduino.D9, R1.Pin_0
  N3: R1.Pin_1, Q1.gate
